# Fritzing sketch Maestro MkIII (saved by Fritzing 0.9.6b)
breadboards: 2

parts:
  L298N1 = L298N DC motor driver
  Raspberry_Pi_1 = Raspberry Pi 3 [part_number=RPI-3-V1.2]
  Grabber = DC Motor  # not connected
  Tapper = DC Motor  # not connected
  M1 = RioRand LM2596
  X1 = USB Connectors [package=usb-microb]

nets:
  N1: L298N1.12V, M1.Pin_1
  N2: L298N1.GND, M1.Pin_2
  N3: L298N1.ENA, Raspberry_Pi_1.GIPO12
  N4: L298N1.ENB, Raspberry_Pi_1.GIPO13
  N5: L298N1.IN1, Raspberry_Pi_1.GIPO7
  N6: L298N1.IN2, Raspberry_Pi_1.ID_SC
  N7: L298N1.IN3, Raspberry_Pi_1.GIPO5
  N8: L298N1.IN4, Raspberry_Pi_1.GIPO6
  N9: M1.Pin_3, X1.GND
  N10: M1.Pin_4, X1.VBUS

custom parts:
  L298N DC motor driver: 2x DC motor driver with 78M05 positive voltage regulator (7..35 V) L298N: max 46 V, 2 A Set 5 V Enable jumper to enable 5 V regultor (needed for the L298N) and +5 V output at screw terminal or supply external +5 V at screw terminal Set ENA and/or ENB to +5 V to enable motor permanently or supply ENA and/or ENB with PWM signal IN1 and IN2 set rotation directory for motor A (OUT1/OUT2) IN2 and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
