# Fritzing sketch Sandbox (saved by Fritzing 0.9.6b)
breadboards: 1

parts:
  Raspberry_Pi_1 = Raspberry Pi 3 [part_number=RPI-3-V1.2]
  R1 = Resistor [tolerance=±5% power=0.25 resistance=220 package=THT]
  LED1 = LED - 5mm [color="Red (633nm)" current=0.030 package="5 mm [THT]"]
  R2 = Resistor [tolerance=±5% power=0.25 resistance=220 package=THT]
  LED2 = LED - 5mm [color="Green (555nm)" current=0.030 package="5 mm [THT]"]
  J1 = Power Jack [package=power_jack_combo]
  M1 = RioRand LM2596
  JP1 = USB_MICROB_PLUG [package=micro-b-th]
  Q1 = NPN-Transistor [package="SOT-23 [SMD]"]
  D1 = Rectifier Diode [package="Melf DO-213 AA [SMD]"]
  R3 = Resistor [tolerance=±5% resistance=220 package="0402 [SMD]"]
  L1 = Solenoid

nets:
  N1: Raspberry_Pi_1.GPIO13, R2.Pin_1
  N2: Raspberry_Pi_1.GPIO26, R1.Pin_0
  N3: Raspberry_Pi_1.GND, LED1.cathode, LED2.cathode, Q1.1
  N4: Raspberry_Pi_1.GPIO23, R3.Pin_0
  N5: R1.Pin_1, LED1.anode
  N6: R2.Pin_0, LED2.anode
  N7: J1.GND, J1.GNDBREAK, M1.Pin_2
  N8: J1.PWR, M1.Pin_1, Q1.0, D1.cathode, L1.pin2
  N9: M1.Pin_3, JP1.D+
  N10: M1.Pin_4, JP1.GND
  N11: Q1.2, R3.Pin_1
  N12: D1.anode, L1.pin1
